# Fritzing sketch Implemetacion_G4 (saved by Fritzing 0.9.4)
breadboards: 1

parts:
  Raspberry_Pi_1 = Raspberry Pi 3 [part_number=RPI-3-V1.2]
  U1 = atmega328 [package=dip]
  LCD1 = LCD screen
  R1 = Resistor [tolerance=±5% resistance=5k package="2512 [SMD]"]
  Q1 = TRANSISTOR_NPN [package=to-92-ammo]
  BAT1 = BC9VPC [package=bc9vpc]
  U5 = RELAY [package=relay-g5q]
  L1 = Solenoid
  U4 = TRANSCHIPTC5747 [package=camera_sfv24r-2st_2]  # not connected
  Keypad4x2 = Keypad Membran 4x4

nets:
  3V3: Raspberry_Pi_1.3v3, Raspberry_Pi_1.5V, U1.RESET, U1.VCC, U1.AVCC, U1.AREF, BAT1.V+, U5.NO, U5.COIL1
  N1: Raspberry_Pi_1.GIPO15, U1.D1_(TX)
  N2: Raspberry_Pi_1.GIPO14, U1.D0_(RX)
  N3: U1.D2, Keypad4x2.Pin3
  N4: U1.D3_(PWM), Keypad4x2.Pin4
  N5: U1.D4, Keypad4x2.Pin5
  N6: U1.D5_(PWM), Keypad4x2.Pin6
  N7: U1.D6_(PWM), Keypad4x2.Pin7
  N8: U1.D7, Keypad4x2.Pin8
  N9: U1.D8, LCD1.DB4
  N10: U1.D9_(PWM), R1.Pin_1
  N11: U1.D10_(PWM), Keypad4x2.Pin1
  N12: U1.A0, LCD1.DB6
  N13: U1.A1, Keypad4x2.Pin2
  N14: U1.A2, LCD1.V0
  N15: U1.A3, LCD1.RS
  N16: U1.A4, LCD1.R/W
  N17: U1.A5, LCD1.E
  N18: LCD1.DB5, Q1.E, BAT1.V-, L1.pin1
  N19: R1.Pin_0, Q1.B
  N20: Q1.C, U5.COIL2
  N21: U5.MAIN, L1.pin2

notes:
  Cerradura Inteligente
  Grupo 4
  - Milena Chiquito
  - Andrés Noboa
  Paralelo 110

custom parts:
  Keypad Membran 4x4: Membrane Keypad 4x4 Matrix
